// Digital circuit lab2_part2.dig as structural Verilog
module lab2_part2 (
  input  in0,
  input  in1,
  input  in2,
  input  in3,
  output seg_a,
  output seg_f,
  output seg_b,
  output seg_g,
  output seg_e,
  output seg_c,
  output seg_d,
  output seg_dp,
  output sign_a,
  output sign_f,
  output sign_b,
  output sign_g,
  output sign_e,
  output sign_c,
  output sign_d,
  output sign_dp
);

  wire _0, _1, _1_t, _2, _2_t, _3, _3_t, _4, _4_t, _5, _5_t, _6, _6_t, _7, _7_t, _8;

  Decoder #(.Selector_Bits(4)) decoder_1 (
    .sel({in3, in2, in1, in0}), .out_0(_0), .out_1(_1_t), .out_2(_2_t), .out_3(_3_t), .out_4(_4_t),
    .out_5(_5_t), .out_6(_6_t), .out_7(_7_t), .out_8(_8), .out_9(_7), .out_10(_6), .out_11(_5), .out_12(_4),
    .out_13(_3), .out_14(_2), .out_15(_1));
  or or_1 (sign_g, _8, _7, _6, _5, _4, _3, _2, _1);
  or or_2 (seg_a, _0, _2_t, _3_t, _5_t, _6_t, _7_t, _2, _3, _5, _6, _7, _8);
  or or_3 (seg_b, _0, _1_t, _2_t, _3_t, _4_t, _7_t, _1, _2, _3, _4, _7, _8);
  or or_4 (seg_c, _0, _1_t, _3_t, _4_t, _5_t, _6_t, _7_t, _1, _3, _4, _5, _6, _7, _8);
  or or_5 (seg_d, _0, _2_t, _3_t, _5_t, _6_t, _2, _3, _5, _6, _8);
  or or_6 (seg_e, _0, _2_t, _6_t, _2, _6, _8);
  or or_7 (seg_f, _0, _4_t, _5_t, _6_t, _4, _5, _6, _8);
  or or_8 (seg_g, _2_t, _3_t, _4_t, _5_t, _6_t, _6, _5, _4, _3, _2, _8);
  Seven_Seg seven_seg_1 (.a(1'b0), .b(1'b0), .c(1'b0), .d(1'b0), .e(1'b0), .f(1'b0), .g(sign_g), .dp(1'b0));
  Seven_Seg seven_seg_2 (.a(seg_a), .b(seg_b), .c(seg_c), .d(seg_d), .e(seg_e), .f(seg_f), .g(seg_g), .dp(1'b0));

  assign seg_dp = 1'b0;
  assign sign_a = 1'b0;
  assign sign_b = 1'b0;
  assign sign_c = 1'b0;
  assign sign_d = 1'b0;
  assign sign_dp = 1'b0;
  assign sign_e = 1'b0;
  assign sign_f = 1'b0;

  // Notes on the sheet:
  //   Interface (do not edit the content inside this box)
  //   Outputs:
  //   Inputs
  //   Sign
  //   Decimal Number
endmodule

/* Test case:
in3 in2 in1 in0  sign_a sign_b sign_c sign_d sign_e sign_f sign_g  seg_a seg_b seg_c seg_d seg_e seg_f seg_g
 0   0   0   0    0      0      0      0      0      0      0       1     1     1     1     1     1     0
*/
